# Fritzing sketch RadioMarellino (saved by Fritzing 1.0.3b)
circuit board: 10.4701cm x 8.18652cm
breadboards: 1

parts:
  ESP32-S3 = ESP32-S2-DevKitC-1 [part_number=ESP32-S2-DevKitC-1]
  Right = Adafruit MAX98357A I2S 3W Class D Amplifier [part_number="Adafruit #3006"]
  +5V = DD4012SA [package=THT]
  Volume = KY-040 Rotary encoder [package="Breakout board"]
  Vin = screw terminal, 2 pins
  R1 = Resistor [tolerance=±5% power=0.25W resistance=220 package=THT]
  R2 = Resistor [tolerance=±5% power=0.25W resistance=220 package=THT]
  R3 = Resistor [tolerance=±5% power=0.25W resistance=220 package=THT]
  Left = Adafruit MAX98357A I2S 3W Class D Amplifier [part_number="Adafruit #3006"]
  Sinto = KY-040 Rotary encoder [package="Breakout board"]
  C1 = Capacitor Polarized [package=panasonic_c]
  C2 = Capacitor Polarized [package=panasonic_c]

nets:
  VCC: ESP32-S3.pin_1, ESP32-S3.pin_2, Volume.Vcc, Sinto.Vcc
  N1: ESP32-S3.pin_4, Sinto.DT
  N2: ESP32-S3.pin_5, Sinto.CLK
  N3: ESP32-S3.pin_15, Volume.SW
  N4: ESP32-S3.pin_16, Sinto.SW
  N5: ESP32-S3.pin_18, Right.DIN, Left.DIN
  N6: ESP32-S3.pin_19, Right.BCLK, R3.Pin_0, Left.BCLK
  N7: ESP32-S3.pin_20, Right.LRCLK, Left.LRCLK
  VIN: ESP32-S3.pin_21, Right.VIN, +5V.pin3, R1.Pin_1, R2.Pin_1, R3.Pin_1, Left.VIN, C1.+, C2.+
  GND: ESP32-S3.pin_22, ESP32-S3.pin_23, ESP32-S3.pin_24, ESP32-S3.pin_44, Right.GND, +5V.pin2, Volume.GND, Vin.pin1, Left.GND, Sinto.GND, C1.-, C2.-
  N8: ESP32-S3.pin_38, Volume.CLK
  N9: ESP32-S3.pin_39, Volume.DT
  N10: Right.SD_MODE, R1.Pin_0
  N11: +5V.pin1, Vin.pin2
  N12: R2.Pin_0, Left.SD_MODE

custom parts:
  ESP32-S2-DevKitC-1: ESP32-S2-DevKitC-1 is an entry-level development board based on ESP32-S2-SOLO (on-board PCB antenna). It is based on the ESP32 microcontroller that boasts Wifi, Bluetooth, Ethernet and Low Power support all in a single chip. (vanepp) Feb 2022: converted to ESP32-S2-DevKitC-1. This module is 44pins long (2x22) and 11 pins width.
  Adafruit MAX98357A I2S 3W Class D Amplifier: Listen to this good news - we now have an all in one digital audio amp breakout board that works incredibly well with the Raspberry Pi! If you're looking for an easy and low cost way to get you digital sound files bumpin' then the MAX08357 I2S Amp Breakout is for you. It takes standard I2S digital audio input and, not only decodes it into analog, but also amplifies it directly into a speaker.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
  DD4012SA: DD4012SA 1A DC 5V 6V 9V 12V 24V to 3.3V 5V DC-DC Step-Down Buck Converter Regulator Module Board.
  KY-040 Rotary encoder: KY-040 Rotary Encoder with switch on breakout borad from AZ Delivery
